# Fritzing sketch circuit laytou (saved by Fritzing 0.9.3b)
perfboards: 1

parts:
  Part1 = Arduino Uno (Rev3)
  R1 = Resistor [tolerance=±5% resistance=2.2k package=THT]
  R2 = Resistor [tolerance=±5% resistance=68 package=THT]
  R3 = Resistor [tolerance=±5% resistance=68 package=THT]
  CONN1 = USB connector [package=THT]
  D1 = Zener Diode [part_number=1N4732A breakdown_voltage=3.6V package="300 mil [THT]"]
  D2 = Zener Diode [part_number=1N4732A breakdown_voltage=3.6V package="300 mil [THT]"]
  J1 = double row male pin header, 20 pins [form="♂ (male)"]  # not connected

nets:
  N1: Part1.D2, R3.Pin_0
  N2: Part1.D3_PWM, R2.Pin_0
  GND: Part1.GND, CONN1.GND, CONN1.chassis5, CONN1.chassis6, D1.anode, D2.anode
  VIN: Part1.VIN, R1.Pin_1, CONN1.5V
  N3: R1.Pin_0, R3.Pin_1, CONN1.d-, D1.cathode
  N4: R2.Pin_1, CONN1.d+, D2.cathode
